# Fritzing sketch circuit diagram (saved by Fritzing 0.9.3b)
breadboards: 1

parts:
  S1 = Custom Red Round Pushbutton
  S2 = Custom Blue Round Pushbutton  # not connected
  U1 = ESP8266 ESP-01 Upgraded WiFi Module [part_number=ESP8266]  # not connected
  Part1 = White Thumb Joystick  # not connected
  LED1 = RGB LED (com. cathode, rbg) [package="5 mm [THT]"]  # not connected
  LED2 = Infrared LED - 5mm [package="5 mm [THT]"]  # not connected
  S3 = Pushbutton [package="[THT]"]
  S4 = Pushbutton [package="[THT]"]
  S5 = Pushbutton [package="[THT]"]
  Part3 = Arduino Uno (Rev3)  # not connected

nets:
  N1: S1.leg0, S1.leg1
  N2: S3.Pin_1, S3.Pin_2, S3.Pin_3, S3.Pin_4
  N3: S4.Pin_1, S4.Pin_2, S4.Pin_3, S4.Pin_4
  N4: S5.Pin_1, S5.Pin_2, S5.Pin_3, S5.Pin_4

custom parts:
  Custom Red Round Pushbutton: A generic pushbutton.
  Custom Blue Round Pushbutton: A generic pushbutton.
  ESP8266 ESP-01 Upgraded WiFi Module: Upgraded Version ESP-01,all Flash are upgraded to 1M byte.Also support Cloud service remote transmission.
  White Thumb Joystick: Description: This is the breakout board for the thumb joystick. Pins are broken out to a 0.1" header and includes 4 mounting holes in the corners. Dimensions: 1" x 1.25"
  Infrared LED - 5mm: A generic infrared LED (~1.2V)
